// Logisim project Processador_Arquitetura.circ as structural Verilog: 4 circuits, main circuit main
module main (
);

  Registrador_4bits registrador_4bits_1 ();  // open: CLK, W0, D0, S
endmodule

module Banco_de_Registradores (
  input  Clk,
  input  W,
  input  [3:0] C
);

  wire demultiplexer_1_out1, demultiplexer_1_out2, demultiplexer_1_out3, demultiplexer_1_out4,
       demultiplexer_1_out5, demultiplexer_1_out6, demultiplexer_1_out7, demultiplexer_1_out8,
       demultiplexer_1_out9, demultiplexer_1_out10, demultiplexer_1_out11, demultiplexer_1_out12,
       demultiplexer_1_out13, demultiplexer_1_out14, demultiplexer_1_out15;

  Demultiplexer #(.select(4)) demultiplexer_1 (
    .out1(demultiplexer_1_out1), .out2(demultiplexer_1_out2), .out3(demultiplexer_1_out3),
    .out4(demultiplexer_1_out4), .out5(demultiplexer_1_out5), .out6(demultiplexer_1_out6),
    .out7(demultiplexer_1_out7), .out8(demultiplexer_1_out8), .out9(demultiplexer_1_out9),
    .out10(demultiplexer_1_out10), .out11(demultiplexer_1_out11), .out12(demultiplexer_1_out12),
    .out13(demultiplexer_1_out13), .out14(demultiplexer_1_out14), .out15(demultiplexer_1_out15), .in(W),
    .sel(C));  // open: out0
  Registrador_32bits registrador_32bits_1 (.W0(1'b1), .D({32{1'b0}}));  // open: CLK, S
  Registrador_32bits registrador_32bits_2 (.W0(demultiplexer_1_out1), .CLK(Clk));  // open: D, S
  Registrador_32bits registrador_32bits_3 (.W0(demultiplexer_1_out2), .CLK(Clk));  // open: D, S
  Registrador_32bits registrador_32bits_4 (.W0(demultiplexer_1_out3), .CLK(Clk));  // open: D, S
  Registrador_32bits registrador_32bits_5 (.W0(demultiplexer_1_out4), .CLK(Clk));  // open: D, S
  Registrador_32bits registrador_32bits_6 (.W0(demultiplexer_1_out5), .CLK(Clk));  // open: D, S
  Registrador_32bits registrador_32bits_7 (.W0(demultiplexer_1_out6), .CLK(Clk));  // open: D, S
  Registrador_32bits registrador_32bits_8 (.W0(demultiplexer_1_out7), .CLK(Clk));  // open: D, S
  Registrador_32bits registrador_32bits_9 (.W0(demultiplexer_1_out8), .CLK(Clk));  // open: D, S
  Registrador_32bits registrador_32bits_10 (.W0(demultiplexer_1_out9), .CLK(Clk));  // open: D, S
  Registrador_32bits registrador_32bits_11 (.W0(demultiplexer_1_out10), .CLK(Clk));  // open: D, S
  Registrador_32bits registrador_32bits_12 (.W0(demultiplexer_1_out11), .CLK(Clk));  // open: D, S
  Registrador_32bits registrador_32bits_13 (.W0(demultiplexer_1_out12), .CLK(Clk));  // open: D, S
  Registrador_32bits registrador_32bits_14 (.W0(demultiplexer_1_out13), .CLK(Clk));  // open: D, S
  Registrador_32bits registrador_32bits_15 (.W0(demultiplexer_1_out14), .CLK(Clk));  // open: D, S
  Registrador_32bits registrador_32bits_16 (.W0(demultiplexer_1_out15), .CLK(Clk));  // open: D, S
endmodule

module Registrador_4bits (
  input  CLK,
  input  W0,
  input  [3:0] D0,
  output [3:0] S
);

  wire multiplexer_1_out, multiplexer_2_out, multiplexer_3_out, multiplexer_4_out;

  Multiplexer multiplexer_1 (.in0(S[0]), .in1(D0[0]), .out(multiplexer_1_out), .sel(W0));
  Multiplexer multiplexer_2 (.in0(S[1]), .in1(D0[1]), .out(multiplexer_2_out), .sel(W0));
  Multiplexer multiplexer_3 (.in0(S[2]), .in1(D0[2]), .out(multiplexer_3_out), .sel(W0));
  Multiplexer multiplexer_4 (.in0(S[3]), .in1(D0[3]), .out(multiplexer_4_out), .sel(W0));
  D_Flip_Flop d_ff_1 (.D(multiplexer_1_out), .clk(CLK), .Q(S[0]));  // open: Qn, preset, reset
  D_Flip_Flop d_ff_2 (.D(multiplexer_2_out), .clk(CLK), .Q(S[1]));  // open: Qn, preset, reset
  D_Flip_Flop d_ff_3 (.D(multiplexer_3_out), .clk(CLK), .Q(S[2]));  // open: Qn, preset, reset
  D_Flip_Flop d_ff_4 (.D(multiplexer_4_out), .clk(CLK), .Q(S[3]));  // open: Qn, preset, reset
endmodule

module Registrador_32bits (
  input  W0,
  input  CLK,
  input  [31:0] D,
  output [31:0] S
);

  Registrador_4bits registrador_4bits_1 (.CLK(CLK), .W0(W0), .D0(D[3:0]), .S(S[3:0]));
  Registrador_4bits registrador_4bits_2 (.CLK(CLK), .W0(W0), .D0(D[7:4]), .S(S[7:4]));
  Registrador_4bits registrador_4bits_3 (.CLK(CLK), .W0(W0), .D0(D[11:8]), .S(S[11:8]));
  Registrador_4bits registrador_4bits_4 (.CLK(CLK), .W0(W0), .D0(D[15:12]), .S(S[15:12]));
  Registrador_4bits registrador_4bits_5 (.CLK(CLK), .W0(W0), .D0(D[19:16]), .S(S[19:16]));
  Registrador_4bits registrador_4bits_6 (.CLK(CLK), .W0(W0), .D0(D[23:20]), .S(S[23:20]));
  Registrador_4bits registrador_4bits_7 (.CLK(CLK), .W0(W0), .D0(D[27:24]), .S(S[27:24]));
  Registrador_4bits registrador_4bits_8 (.CLK(CLK), .W0(W0), .D0(D[31:28]), .S(S[31:28]));
endmodule
